# Fritzing sketch iot-final (saved by Fritzing 1.0.3b)
breadboards: 2

parts:
  A1 = Werner Rothschopf (modified to ESP32-S3-DevKitC dual USB by vanepp Aug 2024)
  Part1 = Adafruit MAX98357A I2S 3W Class D Amplifier [part_number="Adafruit #3006"]
  LCD1 = 2.8" SPI TFT Module [part_number=MSP2807]
  Part2 = INMP441
  Part3 = RFID-RC522-v3
  A2 = MQ-2 breakout
  A3 = L298N DC motor driver
  BAT1 = BC9VPC [package=bc9vpc]
  M1 = DC Motor [voltage_(max)=6V voltage_(min)=3V]
  S1 = Pushbutton [package="[THT]"]
  DHT1 = DHT11 Humitidy and Temperature Sensor (3 pins)
  SW-1 = Vibration sensor module
  Flame_Sensor_Module1 = Flame Sensor Module [part_number="Flame Sensor Module" chip_label=IC package="DIP (Dual Inline) [THT]"]
  Part4 = HC-SR501 Body Sensor Module
  R1 = Photocell (LDR) [power=0.25W dark_resistance_@0.01lx=300kΩ light_resistance_@100lx=400Ω luminance=10lx package=THT]
  R2 = Resistor [tolerance=±5% resistance=10k package="0805 [SMD]"]
  A4 = COB 12V LED strip
  A5 = COB 12V LED strip
  A6 = COB 12V LED strip
  SP1 = SPEAKER [package=pcb_mount_speaker]

nets:
  N1: A1.Pin_1, A1.Pin_2, Part1.VIN, Part1.SD_MODE, LCD1.pin1
  N2: A1.Pin_4, A2.AO
  N3: A1.Pin_5, Part4.OUT
  VCC: A1.Pin_6, Part2.VDD, Part3.3.3V, DHT1.Plus, SW-1.vcc, Flame_Sensor_Module1.VCC, R1.pin_1
  N4: A1.Pin_7, LCD1.pin4
  N5: A1.Pin_8, Part1.DIN
  N6: A1.Pin_9, Part1.BCLK
  N7: A1.Pin_10, Part1.LRCLK
  N8: A1.Pin_11, A3.IN4
  N9: A1.Pin_12, LCD1.pin5
  N10: A1.Pin_14, LCD1.pin8
  N11: A1.Pin_15, LCD1.pin3
  N12: A1.Pin_16, Part3.SDA
  N13: A1.Pin_17, LCD1.pin6, Part3.MOSI
  N14: A1.Pin_18, LCD1.pin7, Part3.SCK
  N15: A1.Pin_19, LCD1.pin9, Part3.MISO
  GND: A1.Pin_22, A1.Pin_23, A1.Pin_24, A1.Pin_44, Part1.GND, LCD1.pin2, Part2.L/R, Part2.GND, Part3.GND, A2.GND, S1.Pin_3, S1.Pin_4, DHT1.Gnd, SW-1.Ground, Flame_Sensor_Module1.GND, Part4.GND, R2.Pin_0
  N16: A1.Pin_25, A3.ENB
  N17: A1.Pin_28, DHT1.Signal
  N18: A1.Pin_29, Flame_Sensor_Module1.DO
  N19: A1.Pin_31, S1.Pin_1, S1.Pin_2
  N20: A1.Pin_35, A3.ENA
  N21: A1.Pin_38, Part2.SD
  N22: A1.Pin_39, Part2.SCK
  N23: A1.Pin_40, Part2.WS
  N24: A1.Pin_41, SW-1.Digital_output
  N25: Part1.VO-, SP1.-
  N26: Part1.VO+, SP1.+
  VCC_2: A2.VCC, A3.5V, A3.+5V-J1, A3.+5V-J2, A3.IN1, Part4.VCC
  N27: A3.OUT1, A4.Pin_1, A4.Pin_4, A5.Pin_1, A5.Pin_4, A6.Pin_1
  N28: A3.OUT2, A4.Pin_2, A4.Pin_3, A5.Pin_2, A5.Pin_3, A6.Pin_2
  N29: A3.12V, BAT1.V+
  N30: A3.GND, BAT1.V-
  N31: A3.OUT3, M1.pin_1
  N32: A3.OUT4, M1.pin_2
  N33: R1.pin_0, R2.Pin_1

custom parts:
  Werner Rothschopf (modified to ESP32-S3-DevKitC dual USB by vanepp Aug 2024): ESP32-S3 ESP32-S3-DevKitC-1 Dual USB development board Pyboard CircuitPython Micropython wifi BLE5.0 ESP32-S3.
  Adafruit MAX98357A I2S 3W Class D Amplifier: Listen to this good news - we now have an all in one digital audio amp breakout board that works incredibly well with the Raspberry Pi! If you're looking for an easy and low cost way to get you digital sound files bumpin' then the MAX08357 I2S Amp Breakout is for you. It takes standard I2S digital audio input and, not only decodes it into analog, but also amplifies it directly into a speaker.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
  2.8" SPI TFT Module: A generic 2.8 inch LCD TFT 320x240 display with touchscreen and SD card slot. Uses the ILI9341 controller, like the Adafruit displays of this size uses.
  INMP441: This is a simple breakout board for the INMP441 I2S MEMS microphone.
  RFID-RC522-v3: A simple China made RFID-RC522 Reader (6x4 cm); do check the pin labels, as this is a MFRC522 based clone.
  MQ-2 breakout: MQ-2 gas sensor
  L298N DC motor driver: This L298N Motor Driver Module is a high power motor driver module for driving DC and Stepper Motors. This module consists of an L298 motor driver IC and a 78M05 5V regulator.
  DHT11 Humitidy and Temperature Sensor (3 pins): DHT11 Humidity and Temperature Sensor (3 pins).
  Vibration sensor module: Single-roller type full induction trigger switch. When no vibration or tilt, the product is ON conduction state, and in the steady state, when a vibration or tilt, the switch will be rendered instantly disconnect the conductive resistance increases, generating a current pulse signal, thereby triggering circuit. The default state of the swith is close Digital output Supply voltage:3.3V-5V On-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
  Flame Sensor Module: A simple fire/flame sensor where you can easily detect fire interfacing with gizduino boards mcu. By reading the Digital output of the sensor, 0 - if there's a on fire, 1 - no fire detected. With 1 meter range detection (max sensitive adjustment. sensor.
  HC-SR501 Body Sensor Module: Pyroelectric Infrared PIR Motion Sensor Detector Module
  COB 12V LED strip: 12V flexible COB LED strip.
  SPEAKER: General speakers.
